// Logisim project cpu8bit.circ as structural Verilog: 2 circuits, main circuit main
module main (
  input  [7:0] in_1,
  input  in_2
);

  wire clock_1_out;
  wire [7:0] adder_1_out, pc_q;

  Clock clock_1 (.out(clock_1_out));
  Register pc (.D(adder_1_out), .Q(pc_q), .clk(clock_1_out), .clr(in_2));  // open: en
  ROM rom_1 (.addr(pc_q), .data(in_1));
  Adder adder_1 (.a(8'h1), .b(pc_q), .out(adder_1_out));  // open: cin, cout
endmodule

module Banco_de_registadores (
  input  [2:0] read_register_1,
  input  [2:0] read_register_2,
  input  [7:0] read_data_1,
  input  [7:0] write_data,
  input  [2:0] write_register,
  input  regwrite,
  input  [7:0] read_data_2,
  input  clock,
  input  clear
);

  wire we0, we1, we2, we3, we4, we5, we6, we7;
  wire [7:0] demultiplexer_2_out0, demultiplexer_2_out1, demultiplexer_2_out2, demultiplexer_2_out3,
       demultiplexer_2_out4, demultiplexer_2_out5, demultiplexer_2_out6, demultiplexer_2_out7, reg0, reg1,
       reg2, reg3, reg4, reg5, reg6, reg7;

  Demultiplexer #(.select(3)) demultiplexer_1 (
    .out0(we0), .out1(we1), .out2(we2), .out3(we3), .out4(we4), .out5(we5), .out6(we6), .out7(we7),
    .in(regwrite), .sel(write_register));
  Demultiplexer #(.select(3), .width(8)) demultiplexer_2 (
    .out0(demultiplexer_2_out0), .out1(demultiplexer_2_out1), .out2(demultiplexer_2_out2),
    .out3(demultiplexer_2_out3), .out4(demultiplexer_2_out4), .out5(demultiplexer_2_out5),
    .out6(demultiplexer_2_out6), .out7(demultiplexer_2_out7), .in(write_data), .sel(write_register));
  Register u_reg0 (.D(demultiplexer_2_out0), .en(we0), .Q(reg0), .clk(clock), .clr(clear));
  Register register_1 (.D(demultiplexer_2_out1), .en(we1), .Q(reg1), .clk(clock), .clr(clear));
  Register register_2 (.D(demultiplexer_2_out2), .en(we2), .Q(reg2), .clk(clock), .clr(clear));
  Register register_3 (.D(demultiplexer_2_out3), .en(we3), .Q(reg3), .clk(clock), .clr(clear));
  Register register_4 (.D(demultiplexer_2_out4), .en(we4), .Q(reg4), .clk(clock), .clr(clear));
  Register register_5 (.D(demultiplexer_2_out5), .en(we5), .Q(reg5), .clk(clock), .clr(clear));
  Register register_6 (.D(demultiplexer_2_out6), .en(we6), .Q(reg6), .clk(clock), .clr(clear));
  Register register_7 (.D(demultiplexer_2_out7), .en(we7), .Q(reg7), .clk(clock), .clr(clear));
  Multiplexer #(.select(3), .width(8)) multiplexer_1 (
    .in0(reg0), .in1(reg1), .in2(reg2), .in3(reg3), .in4(reg4), .in5(reg5), .in6(reg6), .in7(reg7),
    .out(read_data_1), .sel(read_register_1));
  Multiplexer #(.select(3), .width(8)) multiplexer_2 (
    .in0(reg0), .in1(reg1), .in2(reg2), .in3(reg3), .in4(reg4), .in5(reg5), .in6(reg6), .in7(reg7),
    .out(read_data_2), .sel(read_register_2));

  // Other names for the same wires on the sheet: read1[2:0] = read_register_1; read2[2:0] = read_register_2
endmodule
